# Fritzing sketch arduin-nano-wave (saved by Fritzing 0.9.6b)
circuit board: 10cm x 6cm
breadboards: 1

parts:
  Arduino_Nano = Arduino Nano (Rev3.0)
  R1 = Resistor [tolerance=±5% power=0.25 resistance=10k package=THT]
  R2 = Resistor [tolerance=±5% power=0.25 resistance=10k package=THT]
  R3 = Resistor [tolerance=±5% power=0.25 resistance=10k package=THT]
  J1 = Screw terminal - 2 pins [package=THT]
  J2 = Screw terminal - 2 pins [package=THT]
  J3 = Screw terminal - 2 pins [package=THT]
  J4 = Screw terminal - 2 pins [package=THT]
  LED2 = LED - 5mm [color="Yellow (585nm)" current=0.030 package="5 mm [THT]"]
  LED3 = LED - 5mm [color="Green (570nm)" current=0.030 package="5 mm [THT]"]
  LED1 = LED - 5mm [color="Red (633nm)" current=0.030 package="5 mm [THT]"]

nets:
  N1: Arduino_Nano.GND, J3.pin1, J3.pin2, J4.pin2, LED2.cathode, LED3.cathode, LED1.cathode
  N2: Arduino_Nano.D2, LED1.anode
  N3: Arduino_Nano.D3, LED2.anode
  N4: Arduino_Nano.D4, LED3.anode
  N5: Arduino_Nano.D5, R1.Pin_0, J1.pin1
  N6: Arduino_Nano.D6, R2.Pin_0, J1.pin2
  N7: Arduino_Nano.D7, R3.Pin_0, J2.pin1
  N8: Arduino_Nano.5V, R1.Pin_1, R2.Pin_1, R3.Pin_1
